// Logisim project ALU.circ as structural Verilog: 2 circuits, main circuit 1b ALU
module _1b_ALU (
  input  sub,
  input  cin,
  input  A,
  input  B,
  input  [2:0] in_5,
  input  less,
  output result,
  output out_8,
  output set
);

  wire and_1_out, nor_1_out, or_1_out, xor_1_out, xor_2_out;

  xor xor_1 (xor_1_out, B, sub);
  or or_1 (or_1_out, A, B);
  Adder #(.width(1)) adder_1 (.a(A), .b(xor_1_out), .out(set), .cin(cin), .cout(out_8));
  and and_1 (and_1_out, A, B);
  xor xor_2 (xor_2_out, A, B);
  nor nor_1 (nor_1_out, A, B);
  Multiplexer #(.select(3)) multiplexer_1 (
    .in0(and_1_out), .in1(or_1_out), .in2(xor_2_out), .in3(nor_1_out), .in4(set), .in5(less), .out(result),
    .sel(in_5));  // open: in6, in7, en
endmodule

module ALU (
  input  [7:0] in_1,
  input  sub,
  input  [7:0] in_3,
  input  [2:0] op,
  output [7:0] b,
  output out_6
);

  wire _1b_ALU_2_out_8, _1b_ALU_3_out_8, _1b_ALU_4_out_8, _1b_ALU_5_out_8, _1b_ALU_6_out_8, _1b_ALU_7_out_8,
       _1b_ALU_8_set, _1b_ALU_out_8;

  _1b_ALU _1b_ALU (
    .A(in_1[0]), .B(in_3[0]), .less(_1b_ALU_8_set), .result(b[0]), .sub(sub), .cin(sub),
    .out_8(_1b_ALU_out_8), .in_5(op));  // open: set
  _1b_ALU _1b_ALU_2 (
    .A(in_1[1]), .B(in_3[1]), .less(1'b0), .result(b[1]), .sub(sub), .cin(_1b_ALU_out_8),
    .out_8(_1b_ALU_2_out_8));  // open: set, in_5
  _1b_ALU _1b_ALU_3 (
    .A(in_1[2]), .B(in_3[2]), .less(1'b0), .result(b[2]), .sub(sub), .cin(_1b_ALU_2_out_8),
    .out_8(_1b_ALU_3_out_8), .in_5(op));  // open: set
  _1b_ALU _1b_ALU_4 (
    .A(in_1[3]), .B(in_3[3]), .less(1'b0), .result(b[3]), .sub(sub), .cin(_1b_ALU_3_out_8),
    .out_8(_1b_ALU_4_out_8), .in_5(op));  // open: set
  _1b_ALU _1b_ALU_5 (
    .A(in_1[4]), .B(in_3[4]), .less(1'b0), .result(b[5]), .sub(sub), .cin(_1b_ALU_4_out_8),
    .out_8(_1b_ALU_5_out_8), .in_5(op));  // open: set
  _1b_ALU _1b_ALU_6 (
    .A(in_1[5]), .B(in_3[5]), .less(1'b0), .result(b[4]), .sub(sub), .cin(_1b_ALU_5_out_8),
    .out_8(_1b_ALU_6_out_8), .in_5(op));  // open: set
  _1b_ALU _1b_ALU_7 (
    .A(in_1[6]), .B(in_3[6]), .less(1'b0), .result(b[6]), .sub(sub), .cin(_1b_ALU_6_out_8),
    .out_8(_1b_ALU_7_out_8), .in_5(op));  // open: set
  _1b_ALU _1b_ALU_8 (
    .A(in_1[7]), .B(in_3[7]), .less(1'b0), .result(b[7]), .sub(sub), .cin(_1b_ALU_7_out_8),
    .set(_1b_ALU_8_set), .in_5(op));  // open: out_8
  nor nor_1 (out_6, b[0], b[0], b[2], b[3], b[4], b[5], b[6], b[7]);
endmodule
